// Logisim project SAP-1.circ as structural Verilog: 6 circuits, main circuit main
module main (
  input  [7:0] in_1,
  input  PWR,
  input  CLR,
  input  BUS
);

  wire AI, AO, BI, BO, CE, CI, CLK, CO, EO, HLT, II, IO, MI, nCLK, not_1_out, OI, or_1_out, RI, RO, SU;
  wire [3:0] PC_D, RAM_A;
  wire [7:0] BUS_t, OUT, RAM_D, REG_A, REG_B, REG_I, register_2_q, ROM_A, ROM_H, ROM_L;
  wire [7:4] REG_MA;

  or or_1 (or_1_out, RO, not_1_out);
  assign BUS_t = BUS ? in_1 : 8'bz;  // Controlled_Buffer controlled_buffer_1
  Register register_1 (.D(BUS_t), .IN(MI), .CLK(CLK), .CLR(CLR), .OUT(1'b0), .R({REG_MA, RAM_A}));  // open: Q
  RAM #(.addrWidth(4)) ram_1 (.addr(RAM_A), .data(RAM_D), .clk(CLK), .ld(or_1_out), .clr(CLR));  // open: sel
  not not_1 (not_1_out, RI);
  Register register_2 (.D(BUS_t), .IN(II), .Q(register_2_q), .CLK(CLK), .CLR(CLR), .OUT(IO), .R(REG_I));
  Clock clock_1 (.PWR(PWR), .HLT(HLT), .CLK(CLK), .nCLK(nCLK));
  assign RAM_D = RI ? BUS_t : 8'bz;  // Controlled_Buffer controlled_buffer_2
  assign BUS_t = RO ? RAM_D : 8'bz;  // Controlled_Buffer controlled_buffer_3
  assign BUS_t = IO ? {4'b0000, register_2_q[3:0]} : 8'bz;  // Controlled_Buffer controlled_buffer_4
  Program_Counter program_counter_1 (
    .BUS(BUS_t), .CI(CI), .CE(CE), .out_7(BUS_t), .CLK(CLK), .CLR(CLR), .CO(CO), .R(PC_D));
  Register register_3 (.D(BUS_t), .IN(AI), .Q(BUS_t), .CLK(CLK), .CLR(CLR), .OUT(AO), .R(REG_A));
  Arithmatic_Logic_Unit arithmatic_logic_unit_1 (.REG_A(REG_A), .REG_B(REG_B), .EO(EO), .SU(SU), .OUT(BUS_t));
  Register register_4 (.D(BUS_t), .IN(BI), .Q(BUS_t), .CLK(CLK), .CLR(CLR), .OUT(BO), .R(REG_B));
  Register register_5 (.D(BUS_t), .IN(OI), .Q(OUT), .CLK(CLK), .CLR(CLR), .OUT(1'b1));  // open: R
  Control_Logic_Unit control_logic_unit_1 (
    .INSTRUCTION(REG_I), .ADDRESS(ROM_A), .HIGH_WORD(ROM_H), .LOW_WORD(ROM_L), .II(II), .RO(RO), .RI(RI),
    .MI(MI), .CE(CE), .CI(CO), .CO(CI), .HLT(HLT), .OI(OI), .SU(SU), .EO(EO), .BO(BO), .BI(BI), .AO(AO),
    .AI(AI), .IO(IO), .CLK(nCLK));
  Hex_Digit_Display hex_digit_display_1 (.value(BUS_t[7:4]));  // open: dp
  Hex_Digit_Display hex_digit_display_2 (.value(BUS_t[3:0]));  // open: dp
  Hex_Digit_Display hex_digit_display_3 (.value(RAM_A));  // open: dp
  Hex_Digit_Display hex_digit_display_4 (.value(PC_D));  // open: dp
  Hex_Digit_Display hex_digit_display_5 (.value(RAM_D[7:4]));  // open: dp
  Hex_Digit_Display hex_digit_display_6 (.value(REG_MA));  // open: dp
  Hex_Digit_Display hex_digit_display_7 (.value(RAM_A));  // open: dp
  ROM rom_1 (.addr(ROM_A), .data(ROM_H));  // open: sel
  ROM rom_2 (.addr(ROM_A), .data(ROM_L));  // open: sel
  Hex_Digit_Display hex_digit_display_8 (.value(RAM_D[3:0]));  // open: dp
  Hex_Digit_Display hex_digit_display_9 (.value(ROM_A[7:4]));  // open: dp
  Hex_Digit_Display hex_digit_display_10 (.value(REG_I[7:4]));  // open: dp
  Hex_Digit_Display hex_digit_display_11 (.value(REG_I[3:0]));  // open: dp
  Hex_Digit_Display hex_digit_display_12 (.value(ROM_A[3:0]));  // open: dp
  Hex_Digit_Display hex_digit_display_13 (.value(ROM_H[7:4]));  // open: dp
  Hex_Digit_Display hex_digit_display_14 (.value(REG_A[3:0]));  // open: dp
  Hex_Digit_Display hex_digit_display_15 (.value(REG_A[7:4]));  // open: dp
  Hex_Digit_Display hex_digit_display_16 (.value(OUT[7:4]));  // open: dp
  Hex_Digit_Display hex_digit_display_17 (.value(ROM_H[3:0]));  // open: dp
  Hex_Digit_Display hex_digit_display_18 (.value(ROM_L[7:4]));  // open: dp
  Hex_Digit_Display hex_digit_display_19 (.value(OUT[3:0]));  // open: dp
  Hex_Digit_Display hex_digit_display_20 (.value(ROM_L[3:0]));  // open: dp
  Hex_Digit_Display hex_digit_display_21 (.value(REG_B[7:4]));  // open: dp
  Hex_Digit_Display hex_digit_display_22 (.value(REG_B[3:0]));  // open: dp

  // Other names for the same wires on the sheet: REG_MA[3:0] = RAM_A

  // Notes on the sheet:
  //   MAR
  //   IR
  //   RAM
  //   CLU
  //   AR
  //   ALU
  //   PC
  //   BR
  //   OUT
  //   BUS
  //   ADDRESS
  //   PROGRAM
  //   COUNTER
  //   RAM
  //   MEMORY
  //   ADDRESS
  //   REGISTER
  //   contents of rom_1 (hex, n*v repeats v):
  //   28 13 14*0 28 13 8 2 12*0 28 13 8 2 12*0 28 13 14*0 28 13 14*0 28 13 8 4 12*0 28 13 8 4 12*0 28 13 8
  //   2 12*0 28 13 8 2 12*0 28 13 14*0 28 13 14*0 28 13 14*0 28 13 14*0 28 13 40 13*0 28 13 14*0 28 13 80
  //   contents of rom_2 (hex, n*v repeats v):
  //   18*0 80 40 14*0 80 10 14*0 c0 15*0 90 15*0 80 20 14*0 80 8 14*0 80 10 44 13*0 80 10 46 77*0 80 15*0
  //   21
  //   DATA
  //   INSTRUCTION
  //   REGISTER
  //   ADDRESS
  //   ROM
  //   A
  //   REGISTER
  //   DATA
  //   OUTPUT
  //   REGISTER
  //   B
  //   REGISTER
endmodule

module Clock (
  input  PWR,
  input  HLT,
  output CLK,
  output nCLK
);

  wire and_1_out, and_2_out, clock_1_out, not_1_out;

  Clock_part clock_1 (.out(clock_1_out));
  and and_1 (and_1_out, clock_1_out, PWR);
  not not_1 (not_1_out, HLT);
  and and_2 (and_2_out, and_1_out, not_1_out);
  assign CLK = PWR ? and_2_out : 1'bz;  // Controlled_Buffer controlled_buffer_1
  not not_2 (nCLK, CLK);
endmodule

module Register (
  input  [7:0] D,
  input  IN,
  input  CLK,
  input  CLR,
  input  OUT,
  output [7:0] R,
  output [7:0] Q
);

  wire [7:0] controlled_buffer_1_out;

  assign controlled_buffer_1_out = IN ? D : 8'bz;  // Controlled_Buffer controlled_buffer_1
  Register_part register_1 (.D(controlled_buffer_1_out), .en(IN), .Q(R), .clk(CLK), .clr(CLR));
  assign Q = OUT ? R : 8'bz;  // Controlled_Buffer controlled_buffer_2
endmodule

module Program_Counter (
  input  [7:0] BUS,
  input  CI,
  input  CE,
  input  CO,
  input  CLK,
  input  CLR,
  output [7:0] out_7,
  output [3:0] R
);

  wire [3:0] controlled_buffer_1_out;

  assign controlled_buffer_1_out = CI ? BUS[3:0] : 4'bz;  // Controlled_Buffer controlled_buffer_1
  Counter #(.width(4), .max('hf)) counter_1 (
    .load(CI), .D(controlled_buffer_1_out), .count(CE), .Q(R), .clk(CLK), .clr(CLR));  // open: carry
  assign out_7 = CO ? {4'b0000, R} : 8'bz;  // Controlled_Buffer controlled_buffer_2
endmodule

module Arithmatic_Logic_Unit (
  input  [7:0] REG_A,
  input  [7:0] REG_B,
  input  EO,
  input  SU,
  output [7:0] OUT
);

  wire and_1_out, not_1_out;
  wire [7:0] adder_1_out, controlled_buffer_1_out, controlled_buffer_2_out, controlled_buffer_3_out,
       controlled_buffer_4_out, subtractor_1_out;

  assign controlled_buffer_1_out = not_1_out ? REG_A : 8'bz;  // Controlled_Buffer controlled_buffer_1
  assign controlled_buffer_2_out = not_1_out ? REG_B : 8'bz;  // Controlled_Buffer controlled_buffer_2
  not not_1 (not_1_out, SU);
  assign controlled_buffer_3_out = SU ? REG_A : 8'bz;  // Controlled_Buffer controlled_buffer_3
  assign controlled_buffer_4_out = SU ? REG_B : 8'bz;  // Controlled_Buffer controlled_buffer_4
  Adder adder_1 (.a(controlled_buffer_1_out), .b(controlled_buffer_2_out), .out(adder_1_out));  // open: cin, cout
  Subtractor subtractor_1 (
    .a(controlled_buffer_3_out), .b(controlled_buffer_4_out), .out(subtractor_1_out));  // open: bin, bout
  assign OUT = EO ? adder_1_out : 8'bz;  // Controlled_Buffer controlled_buffer_5
  and and_1 (and_1_out, EO, SU);
  assign OUT = and_1_out ? subtractor_1_out : 8'bz;  // Controlled_Buffer controlled_buffer_6
endmodule

module Control_Logic_Unit (
  input  [7:0] INSTRUCTION,
  input  CLK,
  input  [7:0] HIGH_WORD,
  input  [7:0] LOW_WORD,
  output [7:0] ADDRESS,
  output II,
  output RO,
  output RI,
  output MI,
  output CE,
  output CI,
  output CO,
  output HLT,
  output OI,
  output SU,
  output EO,
  output BO,
  output BI,
  output AO,
  output AI,
  output IO
);

  wire decoder_1_out8, T0, T1, T2, T3, T4, T5, T6, T7;

  Counter #(.width(4), .max('hf)) counter_1 (
    .count(1'b1), .Q(ADDRESS[3:0]), .clk(CLK), .clr(decoder_1_out8));  // open: load, D, carry
  Decoder #(.select(4)) decoder_1 (
    .out0(T0), .out1(T1), .out2(T2), .out3(T3), .out4(T4), .out5(T5), .out6(T6), .out7(T7),
    .out8(decoder_1_out8), .sel(ADDRESS[3:0]), .en(1'b1));  // open: out9, out10, out11, out12, out13, out14, out15

  assign ADDRESS[7:4] = INSTRUCTION[7:4];
  assign AI = LOW_WORD[6];
  assign AO = LOW_WORD[5];
  assign BI = LOW_WORD[4];
  assign BO = LOW_WORD[3];
  assign CE = HIGH_WORD[4];
  assign CI = HIGH_WORD[5];
  assign CO = HIGH_WORD[6];
  assign EO = LOW_WORD[2];
  assign HLT = HIGH_WORD[7];
  assign II = HIGH_WORD[0];
  assign IO = LOW_WORD[7];
  assign MI = HIGH_WORD[3];
  assign OI = LOW_WORD[0];
  assign RI = HIGH_WORD[2];
  assign RO = HIGH_WORD[1];
  assign SU = LOW_WORD[1];
endmodule
